// Logisim project CPU.circ as structural Verilog: 1 circuit, main circuit main
module main (
  output [15:0] out_1,
  output [7:0] out_2
);

  wire clock_1_out, not_1_out;
  wire [7:0] counter_1_q, counter_2_q, demultiplexer_1_out1;

  not not_1 (not_1_out, out_1[15]);
  Counter counter_1 (
    .load(not_1_out), .D(out_2), .count(out_1[15]), .Q(counter_1_q), .clk(clock_1_out));  // open: carry, clr
  Clock clock_1 (.out(clock_1_out));
  ROM #(.dataWidth(16)) rom_1 (.addr(counter_1_q), .data(out_1));  // open: sel
  Demultiplexer #(.width(8), .enable("false")) demultiplexer_1 (
    .out0(out_2), .out1(demultiplexer_1_out1), .in(out_1[7:0]), .sel(out_1[15]));
  Counter counter_2 (.Q(counter_2_q), .clk(clock_1_out));  // open: load, D, count, carry, clr
  RAM #(.bus("separate")) ram_1 (
    .addr(counter_2_q), .din(demultiplexer_1_out1), .str(clock_1_out), .clk(clock_1_out));  // open: data, sel, ld, clr

  // Notes on the sheet:
  //   contents of rom_1 (hex, n*v repeats v):
  //   8000 8001 3 8002 e
endmodule
